// Logisim project ULA_8b.circ as structural Verilog: 8 circuits, main circuit main
module main (
  input  [7:0] A,
  input  [7:0] B,
  output [7:0] Out_ULA
);

  And_8b and_8b_1 ();  // open: A, B, S
  Not_8b not_8b_1 ();  // open: A, S
  Or_8b or_8b_1 ();  // open: A, B, S
  Comparador_8b comparador_8b_1 ();  // open: A, B, out_3
  Somador_8b somador_8b_1 ();  // open: A, B, Cin, S, Cout
  ShiftLeft_8b shiftleft_8b_1 ();  // open: A, in_3, Fill, S
  Multiplexer #(.select(3), .width(8)) multiplexer_1 (.out(Out_ULA));  // open: in0, in1, in2, in3, in4, in5, in6, in7, sel
endmodule

module Somador_Completo (
  input  A,
  input  B,
  input  Cin,
  output out_4,
  output out_5
);

  wire and_1_out, and_2_out, and_3_out, xor_1_out;

  xor xor_1 (xor_1_out, A, B);
  and and_1 (and_1_out, A, Cin);
  and and_2 (and_2_out, A, B);
  and and_3 (and_3_out, B, Cin);
  xor xor_2 (out_4, xor_1_out, Cin);
  or or_1 (out_5, and_1_out, and_2_out, and_3_out);
endmodule

module Somador_8b (
  input  Cin,
  input  [7:0] A,
  input  [7:0] B,
  output [7:0] S,
  output Cout
);

  wire somador_completo_1_out_5, somador_completo_2_out_5, somador_completo_3_out_5,
       somador_completo_4_out_5, somador_completo_5_out_5, somador_completo_6_out_5, somador_completo_7_out_5;

  Somador_Completo somador_completo_1 (.A(A[0]), .B(B[0]), .Cin(Cin), .out_5(somador_completo_1_out_5), .out_4(S[0]));
  Somador_Completo somador_completo_2 (
    .A(A[1]), .B(B[1]), .Cin(somador_completo_1_out_5), .out_5(somador_completo_2_out_5), .out_4(S[1]));
  Somador_Completo somador_completo_3 (
    .A(A[2]), .B(B[2]), .Cin(somador_completo_2_out_5), .out_5(somador_completo_3_out_5), .out_4(S[2]));
  Somador_Completo somador_completo_4 (
    .A(A[3]), .B(B[3]), .Cin(somador_completo_3_out_5), .out_5(somador_completo_4_out_5), .out_4(S[3]));
  Somador_Completo somador_completo_5 (
    .A(A[4]), .B(B[4]), .Cin(somador_completo_4_out_5), .out_5(somador_completo_5_out_5), .out_4(S[4]));
  Somador_Completo somador_completo_6 (
    .A(A[5]), .B(B[5]), .Cin(somador_completo_5_out_5), .out_5(somador_completo_6_out_5), .out_4(S[5]));
  Somador_Completo somador_completo_7 (
    .A(A[6]), .B(B[6]), .Cin(somador_completo_6_out_5), .out_5(somador_completo_7_out_5), .out_4(S[6]));
  Somador_Completo somador_completo_8 (.A(A[7]), .B(B[7]), .Cin(somador_completo_7_out_5), .out_5(Cout), .out_4(S[7]));
endmodule

module And_8b (
  input  [7:0] A,
  input  [7:0] B,
  output [7:0] S
);

  and and_1 (S[0], A[0], B[0]);
  and and_2 (S[1], A[1], B[1]);
  and and_3 (S[2], A[2], B[2]);
  and and_4 (S[3], A[3], B[3]);
  and and_5 (S[4], A[4], B[4]);
  and and_6 (S[5], A[5], B[5]);
  and and_7 (S[6], A[6], B[6]);
  and and_8 (S[7], A[7], B[7]);
endmodule

module Not_8b (
  input  [7:0] A,
  output [7:0] S
);

  not not_1 (S[0], A[0]);
  not not_2 (S[1], A[1]);
  not not_3 (S[2], A[2]);
  not not_4 (S[3], A[3]);
  not not_5 (S[4], A[4]);
  not not_6 (S[5], A[5]);
  not not_7 (S[6], A[6]);
  not not_8 (S[7], A[7]);
endmodule

module Or_8b (
  input  [7:0] A,
  input  [7:0] B,
  output [7:0] S
);

  or or_1 (S[0], A[0], B[0]);
  or or_2 (S[1], A[1], B[1]);
  or or_3 (S[2], A[2], B[2]);
  or or_4 (S[3], A[3], B[3]);
  or or_5 (S[4], A[4], B[4]);
  or or_6 (S[5], A[5], B[5]);
  or or_7 (S[6], A[6], B[6]);
  or or_8 (S[7], A[7], B[7]);
endmodule

module ShiftLeft_8b (
  input  [7:0] A,
  input  Fill,
  input  [2:0] in_3,
  output [7:0] S
);

  wire multiplexer_1_out, multiplexer_2_out, multiplexer_3_out, multiplexer_4_out, multiplexer_6_out,
       multiplexer_7_out, multiplexer_9_out, multiplexer_10_out, multiplexer_12_out, multiplexer_13_out,
       multiplexer_15_out, multiplexer_16_out, multiplexer_18_out, multiplexer_19_out, multiplexer_21_out,
       multiplexer_22_out;

  Multiplexer multiplexer_1 (.in0(A[7]), .in1(A[6]), .out(multiplexer_1_out), .sel(in_3[0]));
  Multiplexer multiplexer_2 (.in0(multiplexer_1_out), .in1(multiplexer_6_out), .out(multiplexer_2_out), .sel(in_3[1]));
  Multiplexer multiplexer_3 (.in0(A[6]), .in1(A[5]), .out(multiplexer_3_out), .sel(in_3[0]));
  Multiplexer multiplexer_4 (.in0(multiplexer_3_out), .in1(multiplexer_9_out), .out(multiplexer_4_out), .sel(in_3[1]));
  Multiplexer multiplexer_5 (.in0(multiplexer_2_out), .in1(multiplexer_13_out), .out(S[7]), .sel(in_3[2]));
  Multiplexer multiplexer_6 (.in0(A[5]), .in1(A[4]), .out(multiplexer_6_out), .sel(in_3[0]));
  Multiplexer multiplexer_7 (.in0(multiplexer_6_out), .in1(multiplexer_12_out), .out(multiplexer_7_out), .sel(in_3[1]));
  Multiplexer multiplexer_8 (.in0(multiplexer_4_out), .in1(multiplexer_16_out), .out(S[6]), .sel(in_3[2]));
  Multiplexer multiplexer_9 (.in0(A[4]), .in1(A[3]), .out(multiplexer_9_out), .sel(in_3[0]));
  Multiplexer multiplexer_10 (
    .in0(multiplexer_9_out), .in1(multiplexer_18_out), .out(multiplexer_10_out), .sel(in_3[1]));
  Multiplexer multiplexer_11 (.in0(multiplexer_7_out), .in1(multiplexer_19_out), .out(S[5]), .sel(in_3[2]));
  Multiplexer multiplexer_12 (.in0(A[3]), .in1(A[2]), .out(multiplexer_12_out), .sel(in_3[0]));
  Multiplexer multiplexer_13 (
    .in0(multiplexer_12_out), .in1(multiplexer_21_out), .out(multiplexer_13_out), .sel(in_3[1]));
  Multiplexer multiplexer_14 (.in0(multiplexer_10_out), .in1(multiplexer_22_out), .out(S[4]), .sel(in_3[2]));
  Multiplexer multiplexer_15 (.in0(A[2]), .in1(A[1]), .out(multiplexer_15_out), .sel(in_3[0]));
  Multiplexer multiplexer_16 (.in0(multiplexer_15_out), .in1(Fill), .out(multiplexer_16_out), .sel(in_3[1]));
  Multiplexer multiplexer_17 (.in0(multiplexer_13_out), .in1(Fill), .out(S[3]), .sel(in_3[2]));
  Multiplexer multiplexer_18 (.in0(A[1]), .in1(A[0]), .out(multiplexer_18_out), .sel(in_3[0]));
  Multiplexer multiplexer_19 (.in0(multiplexer_18_out), .in1(Fill), .out(multiplexer_19_out), .sel(in_3[1]));
  Multiplexer multiplexer_20 (.in0(multiplexer_16_out), .in1(Fill), .out(S[2]), .sel(in_3[2]));
  Multiplexer multiplexer_21 (.in0(A[0]), .in1(Fill), .out(multiplexer_21_out), .sel(in_3[0]));
  Multiplexer multiplexer_22 (.in0(multiplexer_21_out), .in1(Fill), .out(multiplexer_22_out), .sel(in_3[1]));
  Multiplexer multiplexer_23 (.in0(multiplexer_19_out), .in1(Fill), .out(S[1]), .sel(in_3[2]));
  Multiplexer multiplexer_24 (.in0(multiplexer_22_out), .in1(Fill), .out(S[0]), .sel(in_3[2]));
endmodule

module Comparador_8b (
  input  [7:0] A,
  input  [7:0] B,
  output out_3
);

  wire xnor_1_out, xnor_2_out, xnor_3_out, xnor_4_out, xnor_5_out, xnor_6_out, xnor_7_out, xnor_8_out;

  xnor xnor_1 (xnor_1_out, A[0], B[0]);
  xnor xnor_2 (xnor_2_out, A[1], B[1]);
  xnor xnor_3 (xnor_3_out, A[2], B[2]);
  xnor xnor_4 (xnor_4_out, A[3], B[3]);
  xnor xnor_5 (xnor_5_out, A[4], B[4]);
  xnor xnor_6 (xnor_6_out, A[5], B[5]);
  xnor xnor_7 (xnor_7_out, A[6], B[6]);
  xnor xnor_8 (xnor_8_out, A[7], B[7]);
  and and_1 (out_3, xnor_1_out, xnor_2_out, xnor_3_out, xnor_4_out, xnor_5_out, xnor_6_out, xnor_7_out, xnor_8_out);
endmodule
